# Fritzing sketch Esp32 controller (saved by Fritzing 1.0.4)
breadboards: 1

parts:
  A1 = ESP32-C6-DevKitC-1
  Part1 = Black Joystick KY-023

nets:
  N1: A1.Pin_1, Part1.+5V
  N2: A1.Pin_7, Part1.VRx
  N3: A1.Pin_8, Part1.VRy
  N4: A1.Pin_15, A1.Pin_18, A1.Pin_32, Part1.GND
  N5: A1.Pin_22, Part1.SW

custom parts:
  ESP32-C6-DevKitC-1: ESP32-C6-DevKitC-1 is an entry-level development board based on ESP32-C6-WROOM-1(U), a general-purpose module with a 8 MB SPI flash. This board integrates complete Wi-Fi, Bluetooth LE, Zigbee, and Thread functions.
  Black Joystick KY-023: Description: The joystick is a combination of 2 analoog potentiometer and a digital switch. Arduino GND --> Module pin - Arduino +5V --> Module pin +5V Arduino Analoog 0 --> Module VRx Arduino Analoog 1 --> Module VRy Arduino Digital --> Module SW Dimensions: 1" x 1.25"
